# Fritzing sketch ov7670_rp2040 (saved by Fritzing 0.9.4)
breadboards: 1

parts:
  Mod1 = Raspberry Pi Pico
  U1 = OV7670 Camera [package=camera_sfv24r-2st_2]
  R1 = Resistor [tolerance=±5% resistance=4.7k package=THT]
  R2 = Resistor [tolerance=±5% resistance=4.7k package=THT]

nets:
  N1: Mod1.pin_3, Mod1.pin_8, Mod1.pin_13, Mod1.pin_18, Mod1.pin_23, Mod1.pin_28, Mod1.pin_33, Mod1.pin_38
  N2: Mod1.pin_12, U1.D1
  N3: Mod1.pin_15, U1.D3
  N4: Mod1.pin_17, U1.D5
  N5: Mod1.pin_20, U1.D7
  N6: Mod1.pin_21, U1.VSYNC
  N7: Mod1.pin_24, U1.PCLK
  N8: Mod1.pin_26, R1.Pin_0
  N9: Mod1.pin_27, U1.SIOC, R2.Pin_0
  N10: Mod1.pin_36, U1.3V3, U1.RESET, R1.Pin_1, R2.Pin_1

custom parts:
  Raspberry Pi Pico: Raspberry Pi Pico. Based around the RP2040 microcontroller the Pico is a low cost microcontroller device bringing Raspberry Pi quality, cost, and easy of use to the microcontroller space. Jan 2021, Split part in to two versions: SMD (this one) and tht. This one is single sided and uses the castellation pads to solder the module to the board (no holes, other than for the USB connector!). The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
  OV7670 Camera: CMOS image sensor
